# Fritzing sketch BlinkLEDschets_0967087 (saved by Fritzing 0.9.3b)
circuit board: 8.46667cm x 5.64444cm

parts:
  WeMos_D1_Mini1 = WeMos D1 Mini
  R1 = Resistor [tolerance=±5% resistance=220 package="0603 [SMD]"]
  LED = LED - 3mm [color="Red (633nm)" package="3 mm [THT]"]

nets:
  N1: WeMos_D1_Mini1.D4, R1.Pin_0
  N2: WeMos_D1_Mini1.G, LED.cathode
  N3: R1.Pin_1, LED.anode
